// Logisim project regfile.circ as structural Verilog: 1 circuit, main circuit regfile
module regfile (
  input  [4:0] ReadIndex1,
  input  [4:0] ReadIndex2,
  input  [4:0] WriteIndex,
  input  [31:0] WriteData,
  input  RegWEn,
  input  clk,
  output [31:0] ra,
  output [31:0] sp,
  output [31:0] t0,
  output [31:0] t1,
  output [31:0] t2,
  output [31:0] s0,
  output [31:0] s1,
  output [31:0] a0,
  output [31:0] ReadData1,
  output [31:0] ReadData2
);

  wire [4:0] Writeindex_t;
  wire [31:0] x0, x3, x4, x11, x12, x13, x14, x15, x16, x17, x18, x19, x20, x21, x22, x23, x24, x25, x26,
       x27, x28, x29, x30, x31;

  Register #(.width(32)) u_x0 (.D({32{1'b0}}), .clk(clk), .Q(x0));  // open: en, clr
  Register #(.width(32)) register_1 (.clk(clk), .Q(ra));  // open: D, en, clr
  Register #(.width(32)) register_2 (.clk(clk), .Q(sp));  // open: D, en, clr
  Register #(.width(32)) register_3 (.clk(clk), .Q(x3));  // open: D, en, clr
  Register #(.width(32)) register_4 (.clk(clk), .Q(x16));  // open: D, en, clr
  Register #(.width(32)) register_5 (.clk(clk), .Q(x17));  // open: D, en, clr
  Register #(.width(32)) register_6 (.clk(clk), .Q(x18));  // open: D, en, clr
  Register #(.width(32)) register_7 (.clk(clk), .Q(x19));  // open: D, en, clr
  Register #(.width(32)) register_8 (.clk(clk), .Q(x4));  // open: D, en, clr
  Register #(.width(32)) register_9 (.clk(clk), .Q(t0));  // open: D, en, clr
  Register #(.width(32)) register_10 (.clk(clk), .Q(t1));  // open: D, en, clr
  Register #(.width(32)) register_11 (.clk(clk), .Q(t2));  // open: D, en, clr
  Register #(.width(32)) register_12 (.clk(clk), .Q(x20));  // open: D, en, clr
  Register #(.width(32)) register_13 (.clk(clk), .Q(x21));  // open: D, en, clr
  Register #(.width(32)) register_14 (.clk(clk), .Q(x22));  // open: D, en, clr
  Register #(.width(32)) register_15 (.clk(clk), .Q(x23));  // open: D, en, clr
  Register #(.width(32)) register_16 (.clk(clk), .Q(s0));  // open: D, en, clr
  Register #(.width(32)) register_17 (.clk(clk), .Q(s1));  // open: D, en, clr
  Register #(.width(32)) register_18 (.clk(clk), .Q(a0));  // open: D, en, clr
  Register #(.width(32)) register_19 (.clk(clk), .Q(x11));  // open: D, en, clr
  Register #(.width(32)) register_20 (.clk(clk), .Q(x24));  // open: D, en, clr
  Register #(.width(32)) register_21 (.clk(clk), .Q(x25));  // open: D, en, clr
  Register #(.width(32)) register_22 (.clk(clk), .Q(x26));  // open: D, en, clr
  Register #(.width(32)) register_23 (.clk(clk), .Q(x27));  // open: D, en, clr
  Register #(.width(32)) register_24 (.clk(clk), .Q(x12));  // open: D, en, clr
  Register #(.width(32)) register_25 (.clk(clk), .Q(x13));  // open: D, en, clr
  Register #(.width(32)) register_26 (.clk(clk), .Q(x14));  // open: D, en, clr
  Register #(.width(32)) register_27 (.clk(clk), .Q(x15));  // open: D, en, clr
  Register #(.width(32)) register_28 (.clk(clk), .Q(x28));  // open: D, en, clr
  Register #(.width(32)) register_29 (.clk(clk), .Q(x29));  // open: D, en, clr
  Register #(.width(32)) register_30 (.clk(clk), .Q(x30));  // open: D, en, clr
  Register #(.width(32)) register_31 (.clk(clk), .Q(x31));  // open: D, en, clr
  Multiplexer #(.select(5), .width(32)) multiplexer_1 (
    .in0(x0), .in1(ra), .in2(sp), .in3(x3), .in4(x4), .in5(t0), .in6(t1), .in7(t2), .in8(s0), .in9(s1),
    .in10(a0), .in11(x11), .in12(x12), .in13(x13), .in14(x14), .in15(x15), .in16(x16), .in17(x17),
    .in18(x18), .in19(x19), .in20(x20), .in21(x21), .in22(x22), .in23(x23), .in24(x24), .in25(x25),
    .in26(x26), .in27(x27), .in28(x28), .in29(x29), .in30(x30), .in31(x31), .out(ReadData1), .sel(ReadIndex1));
  Multiplexer #(.select(5), .width(32)) multiplexer_2 (
    .in0(x0), .in1(ra), .in2(sp), .in3(x3), .in4(x4), .in5(t0), .in6(t1), .in7(t2), .in8(s0), .in9(s1),
    .in10(a0), .in11(x11), .in12(x12), .in13(x13), .in14(x14), .in15(x15), .in16(x16), .in17(x17),
    .in18(x18), .in19(x19), .in20(x20), .in21(x21), .in22(x22), .in23(x23), .in24(x24), .in25(x25),
    .in26(x26), .in27(x27), .in28(x28), .in29(x29), .in30(x30), .in31(x31), .sel(Writeindex_t));  // open: out
  Multiplexer #(.select(5), .width(32)) multiplexer_3 (
    .in0(x0), .in1(ra), .in2(sp), .in3(x3), .in4(x4), .in5(t0), .in6(t1), .in7(t2), .in8(s0), .in9(s1),
    .in10(a0), .in11(x11), .in12(x12), .in13(x13), .in14(x14), .in15(x15), .in16(x16), .in17(x17),
    .in18(x18), .in19(x19), .in20(x20), .in21(x21), .in22(x22), .in23(x23), .in24(x24), .in25(x25),
    .in26(x26), .in27(x27), .in28(x28), .in29(x29), .in30(x30), .in31(x31), .out(ReadData2), .sel(ReadIndex2));

  // Notes on the sheet:
  //   INPUTS to your circuit
  //   DON'T CHANGE THE LOCATIONS OF THE INPUTS AND OUTPUTS!
  //   These are DEBUG/TEST outputs from your circuit.
  //   OUTPUTS from your circuit
endmodule
